# Fritzing sketch schematics (saved by Fritzing 0.9.10b)

parts:
  Part2 = RFID-RC522-v2
  Part3 = LCD1602-I2C
  Keypad4x1 = Keypad Membran 4x4
  U1 = ESP32-38PinWide [part_number=ESP32-38PinWide]
  SG2 = Buzzer 12mm [package=buzzer-12mm-ns]

nets:
  N1: Part2.SDA, U1.GPIO5
  N2: Part2.SCK, U1.GPIO18
  N3: Part2.MOSI, U1.GPIO23
  N4: Part2.MISO, U1.GPIO19
  GND: Part2.GND, Part3.GND, U1.GND, SG2.1
  N5: Part2.RST, U1.GPIO4
  N6: Part2.3.3V, U1.3.3
  VCC: Part3.VCC, U1.VIN
  N7: Part3.SDA, U1.GPIO21
  N8: Part3.SCL, U1.GPIO22
  N9: Keypad4x1.Pin1, U1.GPIO32
  N10: Keypad4x1.Pin2, U1.GPIO33
  N11: Keypad4x1.Pin3, U1.GPIO25
  N12: Keypad4x1.Pin4, U1.GPIO26
  N13: Keypad4x1.Pin5, U1.GPIO27
  N14: Keypad4x1.Pin6, U1.GPIO14
  N15: Keypad4x1.Pin7, U1.GPIO12
  N16: Keypad4x1.Pin8, U1.GPIO13
  N17: U1.GPIO2, SG2.2

custom parts:
  RFID-RC522-v2: A simple China made RFID-RC522 Reader; do check the pin labels, as this is a MFRC522 based clone.
  LCD1602-I2C: A standard character display, usually with 2x16 characters. Comes in many colors with LCM1602 IIC attached.
  Keypad Membran 4x4: Membrane Keypad 4x4 Matrix
  ESP32-38PinWide: Generic 38-Pin ESP32 with wide format (only access to one side of pins on a breadboard) based on Stephen Lilley's HiLetgo ESP-WROOM-32 ESP32 ESP-32S Development Board.
